# Fritzing sketch LEDBedBand (saved by Fritzing 0.9.0b)
circuit board: 5cm x 3.5cm
breadboards: 1

parts:
  MOSFET_G = Basic FET N-Channel [package="TO220 [THT]"]
  MOSFET_R = Basic FET N-Channel [package="TO220 [THT]"]
  R1 = PHOTOCELL [package=photocell-kit]
  LED_Strip = RGB LED - (4 legs) [package="5 mm [THT]"]
  12V_8xAA = Battery
  R2 = Resistor [tolerance=±5% resistance=10k package=THT]
  PIR1 = PIR sensor
  PIR2 = PIR sensor
  VCC1 = Battery
  VCC2 = Battery
  VCC3 = Battery
  U3V50F12_IN = Screw terminal - 2 pins [package=THT]
  U3V50F12_OUT = Screw terminal - 2 pins [package=THT]
  Arduino_Nano = Arduino Nano (Rev3.0)
  MOSFET_B = Basic FET N-Channel [package="TO220 [THT]"]

nets:
  N1: MOSFET_G.gate, Arduino_Nano.D9
  N2: MOSFET_G.drain, LED_Strip.green_cathode
  GND: MOSFET_G.source, MOSFET_R.source, R1.P$2, PIR1.GND, PIR2.GND, VCC1.-, U3V50F12_IN.pin2, U3V50F12_OUT.pin2, Arduino_Nano.GND, MOSFET_B.source
  N3: MOSFET_R.gate, Arduino_Nano.D6
  N4: MOSFET_R.drain, LED_Strip.red_cathode
  N5: R1.P$1, R2.Pin_0, Arduino_Nano.A0
  N6: LED_Strip.common_anode, U3V50F12_OUT.pin1
  N7: LED_Strip.blue_cathode, MOSFET_B.drain
  N8: 12V_8xAA.-, VCC3.+
  N9: 12V_8xAA.+, U3V50F12_IN.pin1, Arduino_Nano.VIN
  V5V: R2.Pin_1, PIR1.VDD, PIR2.VDD, Arduino_Nano.5V
  N10: PIR1.SIG, Arduino_Nano.D2
  N11: PIR2.SIG, Arduino_Nano.D3
  N12: VCC1.+, VCC2.-
  N13: VCC2.+, VCC3.-
  N14: Arduino_Nano.D5, MOSFET_B.gate

notes:
  R
  G
  B
